// Logisim project jja54.circ as structural Verilog: 9 circuits, main circuit main
module main (
);

  wire alu_1_negative, alu_1_zero, CLK, clr, dec7, flWE, halt, inc7, IType, ld, MemWE, neg, ProdSrc, ProdWE,
       put, RegWE, zero;
  wire [1:0] PCSrc;
  wire [2:0] ALUOpp, rd, RegDataSrc, rs, rt;
  wire [3:0] Display_digits_1, Display_digits_2, Display_digits_3, Display_digits_4;
  wire [15:0] ALUout, Data, hi, imm, luiOut, multiplexer_1_out, multiplexer_2_out, multiplexer_3_out, PC_1,
       pc_control_1_output, regHi, regLo, rom_1_data, rsOut, rtOut;

  Clock clock_1 (.out(CLK));
  Hex_Digit_Display hex_digit_display_1 (.value(Display_digits_4));  // open: dp
  // Probe on pc_control_1_output
  PC_Control pc_control_1 (
    .imm(imm), .Target(rsOut), .ret(Data), .Output(pc_control_1_output), .PCSrc(PCSrc), .Halt(halt), .CLK(CLK));
  Hex_Digit_Display hex_digit_display_2 (.value(Display_digits_2));  // open: dp
  Hex_Digit_Display hex_digit_display_3 (.value(Display_digits_3));  // open: dp
  Display Display (
    .Data(rsOut), .WE(put), .Clear(clr), .CLK(CLK), .Digits_1(Display_digits_1), .Digits_2(Display_digits_2),
    .Digits_3(Display_digits_3), .Digits_4(Display_digits_4));
  Adder #(.width(16)) adder_1 (.a(pc_control_1_output), .b(16'h1), .out(PC_1));  // open: cin, cout
  LED u_Halt (.in(halt));
  Hex_Digit_Display hex_digit_display_4 (.value(Display_digits_1));  // open: dp
  ROM #(.addrWidth(16), .dataWidth(16)) rom_1 (.addr(pc_control_1_output), .data(rom_1_data));  // open: sel
  Multiplexer #(.select(3), .width(16)) multiplexer_1 (
    .in0(Data), .in1(ALUout), .in2(luiOut), .in3(rsOut), .in4(imm), .in5(regHi), .in6(regLo),
    .out(multiplexer_1_out), .sel(RegDataSrc));  // open: in7, en
  lui lui_1 (.rsOut(rsOut), .Imm(imm), .luiOut(luiOut));
  Register_File register_file_1 (
    .CLK(CLK), .Data(multiplexer_1_out), .WE(RegWE), .rd(rd), .rs(rs), .rt(rt), .I_Type(IType), .incr7(inc7),
    .decr7(dec7), .rs_out(rsOut), .rt_out(rtOut));
  Control control_1 (
    .Instruction(rom_1_data), .Zero(zero), .Neg(neg), .Halt(halt), .Put(put), .Clear(clr), .Load(ld),
    .I_Type(IType), .ProdSelect(ProdSrc), .flWE(flWE), .RegWE(RegWE), .ProdWE(ProdWE), .MemWE(MemWE),
    .PCSrc(PCSrc), .ALUOp(ALUOpp), .immOut(imm), .RegDataSrc(RegDataSrc), .rd_2(rd), .rt(rt), .rs(rs),
    .rd(rsOut), .Inc7(inc7), .Dec7(dec7));
  Product_Register product_register_1 (
    .HI(hi), .LO(ALUout), .HI_2(regHi), .LO_2(regLo), .WE(ProdWE), .CLK(CLK), .ProdSelect(ProdSrc));  // open: COMBINED
  Multiplexer #(.width(16)) multiplexer_2 (.in0(rtOut), .in1(imm), .out(multiplexer_2_out), .sel(IType));  // open: en
  Multiplexer #(.width(16)) multiplexer_3 (.in0(rtOut), .in1(PC_1), .out(multiplexer_3_out), .sel(IType));  // open: en
  ALU alu_1 (
    .A(rsOut), .B(multiplexer_2_out), .Result(ALUout), .High(hi), .Zero(alu_1_zero),
    .Negative(alu_1_negative), .Operation(ALUOpp));
  FL_Register fl_register_1 (
    .Zero(alu_1_zero), .Neg(alu_1_negative), .flWE(flWE), .Zero_2(zero), .Neg_2(neg), .CLK(CLK));
  RAM #(.addrWidth(16), .dataWidth(16), .bus("separate")) ram_1 (
    .addr(rsOut), .din(multiplexer_3_out), .data(Data), .str(MemWE), .clk(CLK));  // open: sel, ld, clr

  // Notes on the sheet:
  //   contents of rom_1 (hex, n*v repeats v):
  //   800c 700 f818 200 900c c7d8 b810 c860 1000 b010 ffd8 a808 601 9009 1202 1a48 a03 1898 c808 640 2a00
endmodule

module Display (
  input  [15:0] Data,
  input  WE,
  input  Clear,
  input  CLK,
  output [3:0] Digits_1,
  output [3:0] Digits_2,
  output [3:0] Digits_3,
  output [3:0] Digits_4
);

  wire or_1_out;
  wire [15:0] multiplexer_1_out;

  Multiplexer #(.width(16)) multiplexer_1 (
    .in0(Data), .in1({16{1'b0}}), .out(multiplexer_1_out), .sel(Clear));  // open: en
  or or_1 (or_1_out, WE, Clear);
  Register #(.width(16)) register_1 (
    .D(multiplexer_1_out), .en(or_1_out), .Q({Digits_4, Digits_3, Digits_2, Digits_1}), .clk(CLK));  // open: clr
endmodule

module ALU (
  input  [15:0] A,
  input  [15:0] B,
  input  [2:0] Operation,
  output [15:0] Result,
  output [15:0] High,
  output Zero,
  output Negative
);

  wire [15:0] add, \and , left, mul, \not , \or , right, sub;

  Adder #(.width(16)) adder_1 (.a(A), .b(B), .out(add));  // open: cin, cout
  Subtractor #(.width(16)) subtractor_1 (.a(A), .b(B), .out(sub));  // open: bin, bout
  Multiplier #(.width(16)) multiplier_1 (.a(A), .b(B), .out(mul), .cout(High));  // open: cin
  assign \and  = A & B;  // AND_Gate and_1, 16 bits wide
  assign \or  = A | B;  // OR_Gate or_1, 16 bits wide
  assign \not  = ~A;  // NOT_Gate not_1, 16 bits wide
  Shifter #(.width(16)) shifter_1 (.in(A), .\dist (B[3:0]), .out(left));
  Shifter #(.width(16), .shift("lr")) shifter_2 (.in(A), .\dist (B[3:0]), .out(right));
  Multiplexer #(.select(3), .width(16)) multiplexer_1 (
    .in0(add), .in1(sub), .in2(mul), .in3(\and ), .in4(\or ), .in5(\not ), .in6(left), .in7(right),
    .out(Result), .sel(Operation));  // open: en
  Comparator #(.width(16)) comparator_1 (.a(Result), .b({16{1'b0}}), .eq(Zero), .lt(Negative));  // open: gt
endmodule

module Register_File (
  input  CLK,
  input  [15:0] Data,
  input  WE,
  input  [2:0] rd,
  input  [2:0] rs,
  input  [2:0] rt,
  input  I_Type,
  input  incr7,
  input  decr7,
  output [15:0] rs_out,
  output [15:0] rt_out
);

  wire demultiplexer_1_out0, demultiplexer_1_out1, demultiplexer_1_out2, demultiplexer_1_out3,
       demultiplexer_1_out4, demultiplexer_1_out5, demultiplexer_1_out6, demultiplexer_1_out7, or_1_out,
       or_2_out;
  wire [2:0] multiplexer_4_out;
  wire [15:0] multiplexer_1_out, multiplexer_3_out, r0, r1, r2, r3, r4, r5, r6, r7, r7dec, r7inc, r7inpt,
       r7outp, subtractor_2_out;

  Demultiplexer #(.select(3)) demultiplexer_1 (
    .out0(demultiplexer_1_out0), .out1(demultiplexer_1_out1), .out2(demultiplexer_1_out2),
    .out3(demultiplexer_1_out3), .out4(demultiplexer_1_out4), .out5(demultiplexer_1_out5),
    .out6(demultiplexer_1_out6), .out7(demultiplexer_1_out7), .in(WE), .sel(rd));  // open: en
  or or_1 (or_1_out, demultiplexer_1_out7, incr7, decr7);
  Adder #(.width(16)) adder_1 (.a(r7outp), .b(16'h1), .out(r7inc));  // open: cin, cout
  Subtractor #(.width(16)) subtractor_1 (.a(r7outp), .b(16'h1), .out(r7dec));  // open: bin, bout
  Register #(.width(16)) register_1 (.D(Data), .en(demultiplexer_1_out0), .Q(r0), .clk(CLK));  // open: clr
  Register #(.width(16)) register_2 (.D(Data), .en(demultiplexer_1_out1), .Q(r1), .clk(CLK));  // open: clr
  Register #(.width(16)) register_3 (.D(Data), .en(demultiplexer_1_out2), .Q(r2), .clk(CLK));  // open: clr
  Register #(.width(16)) register_4 (.D(Data), .en(demultiplexer_1_out3), .Q(r3), .clk(CLK));  // open: clr
  Register #(.width(16)) register_5 (.D(Data), .en(demultiplexer_1_out4), .Q(r4), .clk(CLK));  // open: clr
  Register #(.width(16)) register_6 (.D(Data), .en(demultiplexer_1_out5), .Q(r5), .clk(CLK));  // open: clr
  Register #(.width(16)) register_7 (.D(Data), .en(demultiplexer_1_out6), .Q(r6), .clk(CLK));  // open: clr
  Register #(.width(16)) register_8 (.D(r7inpt), .en(or_1_out), .Q(r7outp), .clk(CLK));  // open: clr
  Multiplexer #(.width(16)) multiplexer_1 (.in0(Data), .in1(r7inc), .out(multiplexer_1_out), .sel(incr7));  // open: en
  Multiplexer #(.width(16)) multiplexer_2 (
    .in0(multiplexer_1_out), .in1(r7dec), .out(r7inpt), .sel(decr7));  // open: en
  Subtractor #(.width(16)) subtractor_2 (.a(r7outp), .b(16'h1), .out(subtractor_2_out));  // open: bin, bout
  Multiplexer #(.select(3), .width(16)) multiplexer_3 (
    .in0(r0), .in1(r1), .in2(r2), .in3(r3), .in4(r4), .in5(r5), .in6(r6), .in7(r7), .out(multiplexer_3_out),
    .sel(multiplexer_4_out));  // open: en
  or or_2 (or_2_out, incr7, decr7);
  Multiplexer #(.width(3)) multiplexer_4 (.in0(rs), .in1(rd), .out(multiplexer_4_out), .sel(I_Type));  // open: en
  Multiplexer #(.select(3), .width(16)) multiplexer_5 (
    .in0(r0), .in1(r1), .in2(r2), .in3(r3), .in4(r4), .in5(r5), .in6(r6), .in7(r7), .out(rt_out), .sel(rt));  // open: en
  Multiplexer #(.width(16)) multiplexer_6 (.in0(r7outp), .in1(subtractor_2_out), .out(r7), .sel(decr7));  // open: en
  Multiplexer #(.width(16)) multiplexer_7 (
    .in0(multiplexer_3_out), .in1(r7), .out(rs_out), .sel(or_2_out));  // open: en

  // Other names for the same wires on the sheet: itype = I_Type
endmodule

module Product_Register (
  input  ProdSelect,
  input  [15:0] HI,
  input  [15:0] LO,
  input  WE,
  input  CLK,
  output [15:0] HI_2,
  output [31:0] COMBINED,
  output [15:0] LO_2
);

  wire [31:0] adder_1_out, bit_extender_1_out, bit_extender_2_out, regIn, SelectedIn, shifter_1_out;

  assign bit_extender_1_out = {{16{1'b0}}, HI};  // Bit_Extender bit_extender_1
  assign bit_extender_2_out = {{16{1'b0}}, LO};  // Bit_Extender bit_extender_2
  Shifter #(.width(32)) shifter_1 (.in(bit_extender_1_out), .\dist (5'b10000), .out(shifter_1_out));
  assign regIn = shifter_1_out | bit_extender_2_out;  // OR_Gate or_1, 32 bits wide
  Register #(.width(32)) register_1 (.D(SelectedIn), .en(WE), .Q(COMBINED), .clk(CLK));  // open: clr
  Adder #(.width(32)) adder_1 (.a(COMBINED), .b(regIn), .out(adder_1_out));  // open: cin, cout
  Multiplexer #(.width(32)) multiplexer_1 (
    .in0(regIn), .in1(adder_1_out), .out(SelectedIn), .sel(ProdSelect));  // open: en

  assign HI_2 = COMBINED[31:16];
  assign LO_2 = COMBINED[15:0];

  // Other names for the same wires on the sheet: regOut[31:0] = COMBINED
endmodule

module PC_Control (
  input  Halt,
  input  [15:0] imm,
  input  [1:0] PCSrc,
  input  CLK,
  input  [15:0] Target,
  input  [15:0] ret,
  output [15:0] Output
);

  wire not_1_out;
  wire [15:0] adder_1_out, adder_2_out, multiplexer_1_out;

  Adder #(.width(16)) adder_1 (.a(Output), .b(16'h1), .out(adder_1_out));  // open: cin, cout
  Adder #(.width(16)) adder_2 (.a(adder_1_out), .b(imm), .out(adder_2_out));  // open: cin, cout
  Multiplexer #(.select(2), .width(16)) multiplexer_1 (
    .in0(adder_1_out), .in1(adder_2_out), .in2(Target), .in3(ret), .out(multiplexer_1_out), .sel(PCSrc));  // open: en
  not not_1 (not_1_out, Halt);
  Register #(.width(16)) register_1 (.D(multiplexer_1_out), .en(not_1_out), .Q(Output), .clk(CLK));  // open: clr
endmodule

module Control (
  input  [15:0] Instruction,
  input  Zero,
  input  Neg,
  input  [15:0] rd,
  output Halt,
  output Put,
  output Clear,
  output Load,
  output I_Type,
  output ProdSelect,
  output flWE,
  output RegWE,
  output [2:0] rd_2,
  output [2:0] rt,
  output [2:0] rs,
  output ProdWE,
  output MemWE,
  output [1:0] PCSrc,
  output [2:0] ALUOp,
  output [15:0] immOut,
  output [2:0] RegDataSrc,
  output Inc7,
  output Dec7
);

  wire add, adi, \and , and_1_out, and_2_out, and_3_out, and_4_out, and_5_out, and_6_out, and_7_out,
       and_8_out, ani, b, beq, bez, bge, blt, bne, bnz, call, cmp, comparator_2_gt, comparator_3_gt, cpi, jr,
       li, lui, mfhi, mflo, mov, mul, \not , not_1_out, \or , or_1_out, or_2_out, or_3_out, or_5_out,
       or_6_out, or_7_out, or_8_out, or_11_out, or_12_out, or_16_out, ori, pop, push, rd_t, ret, shl, shr,
       sli, sri, st, sub;
  wire [15:0] bit_extender_1_out, bit_extender_2_out;

  Demultiplexer #(.select(5)) demultiplexer_1 (
    .out0(Halt), .out1(Put), .out2(Clear), .out3(mov), .out4(mfhi), .out5(mflo), .out6(Load), .out7(st),
    .out8(push), .out9(pop), .out10(add), .out11(sub), .out12(cmp), .out13(mul), .out14(ProdSelect),
    .out15(\and ), .out16(\or ), .out17(\not ), .out18(shl), .out19(shr), .out20(jr), .out21(ret),
    .in(not_1_out), .sel(Instruction[13:9]));  // open: out22, out23, out24, out25, out26, out27, out28, out29, out30, out31, en
  not not_1 (not_1_out, Instruction[15]);
  Comparator #(.width(16), .mode("unsigned")) comparator_1 (.a(rd), .b({16{1'b0}}), .eq(rd_t));  // open: gt, lt
  Demultiplexer #(.select(4)) demultiplexer_2 (
    .out0(li), .out1(lui), .out2(adi), .out3(ani), .out4(ori), .out5(sli), .out6(sri), .out7(cpi), .out8(b),
    .out9(blt), .out10(bge), .out11(beq), .out12(bne), .out13(bez), .out14(bnz), .out15(call),
    .in(Instruction[15]), .sel(Instruction[14:11]));  // open: en
  Comparator #(.width(3), .mode("unsigned")) comparator_2 (
    .a(ALUOp), .b(3'b000), .gt(comparator_2_gt));  // open: eq, lt
  Comparator #(.width(3), .mode("unsigned")) comparator_3 (
    .a(ALUOp), .b(3'b000), .gt(comparator_3_gt));  // open: eq, lt
  or or_1 (or_1_out, add, adi);
  and and_1 (and_1_out, comparator_2_gt, ~mul, ~cmp, ~cpi);  // AND_Gate
  assign bit_extender_1_out = {{8{Instruction[10]}}, Instruction[10:3]};  // Bit_Extender bit_extender_1
  or or_2 (or_2_out, li, ani, ori);
  assign bit_extender_2_out = {{8{1'b0}}, Instruction[10:3]};  // Bit_Extender bit_extender_2
  or or_3 (or_3_out, comparator_3_gt, or_1_out);
  and and_2 (and_2_out, or_3_out, ~mul);  // AND_Gate
  or or_4 (RegWE, pop, and_1_out, add, adi, Load, li, mov, mfhi, mflo, lui);
  or or_5 (or_5_out, sub, cmp, cpi);
  or or_6 (or_6_out, mul, ProdSelect);
  or or_7 (or_7_out, \and , ani);
  or or_8 (or_8_out, \or , ori);
  Multiplexer #(.width(16)) multiplexer_1 (
    .in0(bit_extender_1_out), .in1(bit_extender_2_out), .out(immOut), .sel(or_2_out));  // open: en
  or or_9 (ProdWE, mul, ProdSelect);
  or or_10 (MemWE, push, st, call);
  or or_11 (or_11_out, shl, sli);
  or or_12 (or_12_out, shr, sri);
  Priority_Encoder priority_encoder_1 (
    .in0(1'b1), .in1(and_2_out), .in2(lui), .in3(mov), .in4(li), .in5(mfhi), .in6(mflo), .out(RegDataSrc));  // open: in7, en_in, gs, en_out
  or or_13 (Inc7, pop, ret);
  or or_14 (Dec7, push, call);
  or or_15 (flWE, add, sub, cmp, adi, cpi);
  Priority_Encoder priority_encoder_2 (
    .in0(1'b1), .in1(or_5_out), .in2(or_6_out), .in3(or_7_out), .in4(or_8_out), .in5(\not ), .in6(or_11_out),
    .in7(or_12_out), .out(ALUOp));  // open: en_in, gs, en_out
  and and_3 (and_3_out, bge, ~Neg);  // AND_Gate
  and and_4 (and_4_out, bne, ~Zero);  // AND_Gate
  and and_5 (and_5_out, blt, Neg);
  and and_6 (and_6_out, beq, Zero);
  and and_7 (and_7_out, bez, rd_t);
  and and_8 (and_8_out, bnz, ~rd_t);  // AND_Gate
  or or_16 (or_16_out, b, and_5_out, and_3_out, and_6_out, and_4_out, and_7_out, and_8_out, call);
  Priority_Encoder #(.select(2)) priority_encoder_3 (
    .in0(1'b1), .in1(or_16_out), .in2(jr), .in3(ret), .out(PCSrc));  // open: gs, en_out, en_in

  assign I_Type = Instruction[15];
  assign rd_2 = Instruction[2:0];
  assign rs = Instruction[8:6];
  assign rt = Instruction[5:3];

  // Other names for the same wires on the sheet: _9 = Instruction[9]; imm[7:0] = Instruction[10:3];
  //   _10 = Instruction[10]; _11 = Instruction[11]; _12 = Instruction[12]; _13 = Instruction[13];
  //   _14 = Instruction[14]; ALUout[2:0] = ALUOp; clr = Clear; _0 = Instruction[0]; _1 = Instruction[1];
  //   _2 = Instruction[2]; _3 = Instruction[3]; _4 = Instruction[4]; _5 = Instruction[5]; _15 = Instruction[15];
  //   ld = Load; mac = ProdSelect; _6 = Instruction[6]; _7 = Instruction[7]; _8 = Instruction[8]

  // Notes on the sheet:
  //   DECODING
  //   R-Type
  //   I-Type:
  //   data
  //   add
endmodule

module lui (
  input  [15:0] rsOut,
  input  [15:0] Imm,
  output [15:0] luiOut
);


  assign luiOut = {Imm[7:0], rsOut[7:0]};
endmodule

module FL_Register (
  input  Zero,
  input  CLK,
  input  Neg,
  input  flWE,
  output Zero_2,
  output Neg_2
);

  Register #(.width(1)) register_1 (.D(Zero), .en(flWE), .Q(Zero_2), .clk(CLK));  // open: clr
  Register #(.width(1)) register_2 (.D(Neg), .en(flWE), .Q(Neg_2), .clk(CLK));  // open: clr

  // Other names for the same wires on the sheet: we = flWE
endmodule
