// Logisim project jja54_controltest.circ as structural Verilog: 8 circuits, main circuit main
module main (
  input  [15:0] Data
);

  wire clock_1_out, clr, WE;
  wire [3:0] Display_digits_1, Display_digits_2, Display_digits_3, Display_digits_4;
  wire [15:0] rom_1_data;

  Clock clock_1 (.out(clock_1_out));
  Hex_Digit_Display hex_digit_display_1 (.value(Display_digits_1));  // open: dp
  Hex_Digit_Display hex_digit_display_2 (.value(Display_digits_2));  // open: dp
  Control control_1 (
    .Clear(clr), .MemWE(WE));  // open: Instruction, R_op, I_op, imm, rd, rt, imm_2, rs, R_op_2, I_op_2, Halt, Put, Load, PCSrc, ALUOp, immOut
  Hex_Digit_Display hex_digit_display_3 (.value(Display_digits_3));  // open: dp
  Hex_Digit_Display hex_digit_display_4 (.value(Display_digits_4));  // open: dp
  Display Display (
    .Data(Data), .WE(WE), .Clear(clr), .CLK(clock_1_out), .Digits_1(Display_digits_1),
    .Digits_2(Display_digits_2), .Digits_3(Display_digits_3), .Digits_4(Display_digits_4));
  LED Halt ();  // open: in
  Register_File register_file_1 ();  // open: CLK, Data, WE, rd, rs, rt, I_Type, incr7, decr7, rs_out, rt_out
  ROM #(.addrWidth(16), .dataWidth(16)) rom_1 (.data(rom_1_data));  // open: addr, sel
  RAM #(.addrWidth(16), .dataWidth(16), .bus("separate")) ram_1 ();  // open: addr, din, data, str, sel, clk, ld, clr
  Ins_Decoder ins_decoder_1 (.Instruction(rom_1_data));  // open: rd, rt, imm, rs, R_op, I_op
  ALU alu_1 ();  // open: A, B, Result, High, Zero, Negative, Operation
endmodule

module Display (
  input  [15:0] Data,
  input  WE,
  input  Clear,
  input  CLK,
  output [3:0] Digits_1,
  output [3:0] Digits_2,
  output [3:0] Digits_3,
  output [3:0] Digits_4
);

  wire and_1_out, not_1_out;

  not not_1 (not_1_out, Clear);
  and and_1 (and_1_out, WE, not_1_out);
  Register #(.width(16)) register_1 (
    .D(Data), .en(and_1_out), .Q({Digits_4, Digits_3, Digits_2, Digits_1}), .clk(CLK));  // open: clr
endmodule

module ALU (
  input  [15:0] A,
  input  [15:0] B,
  input  [2:0] Operation,
  output [15:0] Result,
  output [15:0] High,
  output Zero,
  output Negative
);

  wire [15:0] add, \and , left, mul, \not , \or , right, sub;

  Adder #(.width(16)) adder_1 (.a(A), .b(B), .out(add));  // open: cin, cout
  Subtractor #(.width(16)) subtractor_1 (.a(A), .b(B), .out(sub));  // open: bin, bout
  Multiplier #(.width(16)) multiplier_1 (.a(A), .b(B), .out(mul), .cout(High));  // open: cin
  assign \and  = A & B;  // AND_Gate and_1, 16 bits wide
  assign \or  = A | B;  // OR_Gate or_1, 16 bits wide
  assign \not  = ~A;  // NOT_Gate not_1, 16 bits wide
  Shifter #(.width(16)) shifter_1 (.in(A), .\dist (B[3:0]), .out(left));
  Shifter #(.width(16), .shift("lr")) shifter_2 (.in(A), .\dist (B[3:0]), .out(right));
  Multiplexer #(.select(3), .width(16)) multiplexer_1 (
    .in0(add), .in1(sub), .in2(mul), .in3(\and ), .in4(\or ), .in5(\not ), .in6(left), .in7(right),
    .out(Result), .sel(Operation));  // open: en
  Comparator #(.width(16)) comparator_1 (.a(Result), .b({16{1'b0}}), .eq(Zero), .lt(Negative));  // open: gt
endmodule

module Register_File (
  input  CLK,
  input  [15:0] Data,
  input  WE,
  input  [2:0] rd,
  input  [2:0] rs,
  input  [2:0] rt,
  input  I_Type,
  input  incr7,
  input  decr7,
  output [15:0] rs_out,
  output [15:0] rt_out
);

  wire demultiplexer_1_out0, demultiplexer_1_out1, demultiplexer_1_out2, demultiplexer_1_out3,
       demultiplexer_1_out4, demultiplexer_1_out5, demultiplexer_1_out6, demultiplexer_1_out7, or_1_out;
  wire [2:0] multiplexer_4_out;
  wire [15:0] multiplexer_1_out, r0, r1, r2, r3, r4, r5, r6, r7, r7dec, r7inc, r7inpt, r7outp,
       subtractor_2_out;

  Demultiplexer #(.select(3)) demultiplexer_1 (
    .out0(demultiplexer_1_out0), .out1(demultiplexer_1_out1), .out2(demultiplexer_1_out2),
    .out3(demultiplexer_1_out3), .out4(demultiplexer_1_out4), .out5(demultiplexer_1_out5),
    .out6(demultiplexer_1_out6), .out7(demultiplexer_1_out7), .in(WE), .sel(rd));  // open: en
  or or_1 (or_1_out, demultiplexer_1_out7, incr7, decr7);
  Adder #(.width(16)) adder_1 (.a(r7outp), .b(16'h1), .out(r7inc));  // open: cin, cout
  Subtractor #(.width(16)) subtractor_1 (.a(r7outp), .b(16'h1), .out(r7dec));  // open: bin, bout
  Register #(.width(16)) register_1 (.D(Data), .en(demultiplexer_1_out0), .Q(r0), .clk(CLK));  // open: clr
  Register #(.width(16)) register_2 (.D(Data), .en(demultiplexer_1_out1), .Q(r1), .clk(CLK));  // open: clr
  Register #(.width(16)) register_3 (.D(Data), .en(demultiplexer_1_out2), .Q(r2), .clk(CLK));  // open: clr
  Register #(.width(16)) register_4 (.D(Data), .en(demultiplexer_1_out3), .Q(r3), .clk(CLK));  // open: clr
  Register #(.width(16)) register_5 (.D(Data), .en(demultiplexer_1_out4), .Q(r4), .clk(CLK));  // open: clr
  Register #(.width(16)) register_6 (.D(Data), .en(demultiplexer_1_out5), .Q(r5), .clk(CLK));  // open: clr
  Register #(.width(16)) register_7 (.D(Data), .en(demultiplexer_1_out6), .Q(r6), .clk(CLK));  // open: clr
  Register #(.width(16)) register_8 (.D(r7inpt), .en(or_1_out), .Q(r7outp), .clk(CLK));  // open: clr
  Multiplexer #(.width(16)) multiplexer_1 (.in0(Data), .in1(r7inc), .out(multiplexer_1_out), .sel(incr7));  // open: en
  Multiplexer #(.width(16)) multiplexer_2 (
    .in0(multiplexer_1_out), .in1(r7dec), .out(r7inpt), .sel(decr7));  // open: en
  Subtractor #(.width(16)) subtractor_2 (.a(r7outp), .b(16'h1), .out(subtractor_2_out));  // open: bin, bout
  Multiplexer #(.select(3), .width(16)) multiplexer_3 (
    .in0(r0), .in1(r1), .in2(r2), .in3(r3), .in4(r4), .in5(r5), .in6(r6), .in7(r7), .out(rs_out),
    .sel(multiplexer_4_out));  // open: en
  Multiplexer #(.width(3)) multiplexer_4 (.in0(rs), .in1(rd), .out(multiplexer_4_out), .sel(I_Type));  // open: en
  Multiplexer #(.select(3), .width(16)) multiplexer_5 (
    .in0(r0), .in1(r1), .in2(r2), .in3(r3), .in4(r4), .in5(r5), .in6(r6), .in7(r7), .out(rt_out), .sel(rt));  // open: en
  Multiplexer #(.width(16)) multiplexer_6 (.in0(r7outp), .in1(subtractor_2_out), .out(r7), .sel(decr7));  // open: en

  // Other names for the same wires on the sheet: itype = I_Type
endmodule

module Product_Register (
  input  [15:0] HI,
  input  [15:0] LO,
  input  CLK,
  output [31:0] COMBINED
);

  wire [31:0] bit_extender_1_out, bit_extender_2_out, or_1_out, shifter_1_out;

  Shifter #(.width(32)) shifter_1 (.in(bit_extender_1_out), .\dist (5'b10000), .out(shifter_1_out));
  assign bit_extender_1_out = {{16{1'b0}}, HI};  // Bit_Extender bit_extender_1
  assign bit_extender_2_out = {{16{1'b0}}, LO};  // Bit_Extender bit_extender_2
  assign or_1_out = shifter_1_out | bit_extender_2_out;  // OR_Gate or_1, 32 bits wide
  Register #(.width(32)) register_1 (.D(or_1_out), .Q(COMBINED), .clk(CLK));  // open: en, clr
endmodule

module PC_Control (
  input  Halt,
  input  [7:0] imm,
  input  CLK,
  input  [15:0] Target,
  input  Jump,
  input  Branch,
  input  Zero,
  input  Neg,
  output [15:0] Output
);

  wire and_1_out, not_1_out, not_2_out, not_3_out, or_1_out;
  wire [1:0] and_3_out;
  wire [15:0] adder_1_out, adder_2_out, bit_extender_1_out, multiplexer_1_out;

  Adder #(.width(16)) adder_1 (.a(Output), .b(16'h1), .out(adder_1_out));  // open: cin, cout
  or or_1 (or_1_out, Zero, Neg);
  assign bit_extender_1_out = {{8{imm[7]}}, imm};  // Bit_Extender bit_extender_1
  not not_1 (not_1_out, and_1_out);
  not not_2 (not_2_out, Jump);
  and and_1 (and_1_out, Branch, or_1_out);
  Adder #(.width(16)) adder_2 (.a(adder_1_out), .b(bit_extender_1_out), .out(adder_2_out));  // open: cin, cout
  and and_2 (and_3_out[1], Jump, not_1_out);
  and and_3 (and_3_out[0], not_2_out, and_1_out);
  Multiplexer #(.select(2), .width(16)) multiplexer_1 (
    .in0(adder_1_out), .in1(adder_2_out), .in2(Target), .out(multiplexer_1_out), .sel(and_3_out));  // open: in3, en
  not not_3 (not_3_out, Halt);
  Register #(.width(16)) register_1 (.D(multiplexer_1_out), .en(not_3_out), .Q(Output), .clk(CLK));  // open: clr
endmodule

module Control (
  input  [15:0] Instruction,
  input  [6:0] R_op,
  input  [4:0] I_op,
  input  [7:0] imm,
  output Halt,
  output Put,
  output Clear,
  output Load,
  output MemWE,
  output [1:0] PCSrc,
  output [2:0] rt,
  output [2:0] rs,
  output [6:0] R_op_2,
  output [2:0] ALUOp,
  output [2:0] rd,
  output [7:0] imm_2,
  output [4:0] I_op_2,
  output [15:0] immOut
);

  wire add, adi, \and , ani, b, beq, bez, bge, blt, bne, bnz, call, cmp, cpi, jr, li, lui, mac, mfhi, mflo,
       mov, mul, \not , \or , or_1_out, or_2_out, ori, pop, push, ret, shl, shr, sli, sri, st, sub;
  wire [15:0] bit_extender_1_out, bit_extender_2_out;

  Demultiplexer #(.select(5)) demultiplexer_1 (
    .out0(Halt), .out1(Put), .out2(Clear), .out3(mov), .out4(mfhi), .out5(mflo), .out6(Load), .out7(st),
    .out8(push), .out9(pop), .out10(add), .out11(sub), .out12(cmp), .out13(mul), .out14(mac), .out15(\and ),
    .out16(\or ), .out17(\not ), .out18(shl), .out19(shr), .out20(jr), .out21(ret), .in(1'b1), .sel(R_op[4:0]));  // open: out22, out23, out24, out25, out26, out27, out28, out29, out30, out31, en
  Demultiplexer #(.select(4)) demultiplexer_2 (
    .out0(li), .out1(lui), .out2(adi), .out3(ani), .out4(ori), .out5(sli), .out6(sri), .out7(cpi), .out8(b),
    .out9(blt), .out10(bge), .out11(beq), .out12(bne), .out13(bez), .out14(bnz), .out15(call), .in(1'b1),
    .sel(I_op[3:0]));  // open: en
  or or_1 (or_1_out, sub, cmp);
  or or_2 (or_2_out, mul, mac);
  assign bit_extender_1_out = {{8{1'b0}}, imm};  // Bit_Extender bit_extender_1
  Multiplexer #(.width(16)) multiplexer_1 (
    .in0(bit_extender_1_out), .in1(bit_extender_2_out), .out(immOut));  // open: sel, en
  assign bit_extender_2_out = {{8{imm[7]}}, imm};  // Bit_Extender bit_extender_2
  or or_3 (MemWE, push, st, call);
  Priority_Encoder #(.select(2)) priority_encoder_1 (
    .in0(1'b1), .in1(jr), .in2(ret), .out(PCSrc));  // open: in3, gs, en_out, en_in
  Priority_Encoder priority_encoder_2 (
    .in0(1'b1), .in1(or_1_out), .in2(or_2_out), .in3(\and ), .in4(\or ), .in5(\not ), .in6(shl), .in7(shr),
    .out(ALUOp));  // open: en_in, gs, en_out

  assign I_op_2 = Instruction[15:11];
  assign imm_2 = Instruction[10:3];
  assign R_op_2 = Instruction[15:9];
  assign rd = Instruction[2:0];
  assign rs = Instruction[8:6];
  assign rt = Instruction[5:3];

  // Other names for the same wires on the sheet: clr = Clear; _11 = Instruction[11]; _12 = Instruction[12];
  //   _13 = Instruction[13]; _14 = Instruction[14]; _15 = Instruction[15]; _3 = Instruction[3]; _4 = Instruction[4];
  //   _5 = Instruction[5]; _6 = Instruction[6]; _7 = Instruction[7]; _8 = Instruction[8]; _0 = Instruction[0];
  //   _1 = Instruction[1]; _2 = Instruction[2]; ld = Load; _9 = Instruction[9]; _10 = Instruction[10]

  // Notes on the sheet:
  //   R-Type:
  //   I-Type:
  //   R-Type
  //   add
endmodule

module Ins_Decoder (
  input  [15:0] Instruction,
  output [2:0] rt,
  output [2:0] rs,
  output [6:0] R_op,
  output [2:0] rd,
  output [7:0] imm,
  output [4:0] I_op
);


  assign I_op = Instruction[15:11];
  assign imm = Instruction[10:3];
  assign R_op = Instruction[15:9];
  assign rd = Instruction[2:0];
  assign rs = Instruction[8:6];
  assign rt = Instruction[5:3];

  // Other names for the same wires on the sheet: _11 = Instruction[11]; _12 = Instruction[12]; _13 = Instruction[13];
  //   _14 = Instruction[14]; _15 = Instruction[15]; _3 = Instruction[3]; _4 = Instruction[4]; _5 = Instruction[5];
  //   _6 = Instruction[6]; _7 = Instruction[7]; _8 = Instruction[8]; _9 = Instruction[9]; _10 = Instruction[10];
  //   _0 = Instruction[0]; _1 = Instruction[1]; _2 = Instruction[2]

  // Notes on the sheet:
  //   R-Type:
  //   I-Type:
endmodule
