// Logisim project jja54_lab6.circ as structural Verilog: 2 circuits, main circuit main
module main (
);

  wire CLK, kmap_1_q, not_1_out;
  wire [3:0] adder_1_out, Counter_q;
  wire [7:0] _0s_q, _1s_q, adder_2_out, adder_3_out;

  Clock clock_1 (.out(CLK));
  Register #(.width(4)) Counter (.D(adder_1_out), .Q(Counter_q), .clk(CLK));  // open: en, clr
  Adder #(.width(4)) adder_1 (.a(Counter_q), .b(4'b0001), .out(adder_1_out));  // open: cin, cout
  kmap kmap_1 (.A(Counter_q[0]), .B(Counter_q[1]), .C(Counter_q[2]), .D(Counter_q[3]), .Q(kmap_1_q));
  not not_1 (not_1_out, kmap_1_q);
  Register _1s (.D(adder_2_out), .en(kmap_1_q), .Q(_1s_q), .clk(CLK));  // open: clr
  Register #(.trigger("falling")) _0s (.D(adder_3_out), .en(not_1_out), .Q(_0s_q), .clk(CLK));  // open: clr
  Adder adder_2 (.a(_1s_q), .b(8'h1), .out(adder_2_out));  // open: cin, cout
  Adder adder_3 (.a(_0s_q), .b(8'h1), .out(adder_3_out));  // open: cin, cout
endmodule

module kmap (
  input  A,
  input  B,
  input  C,
  input  D,
  output Q
);

  wire and_1_out, and_2_out, and_3_out, and_4_out;

  and and_1 (and_1_out, B, D);
  and and_2 (and_2_out, ~B, ~D);  // AND_Gate
  and and_3 (and_3_out, ~A, ~C);  // AND_Gate
  and and_4 (and_4_out, ~B, ~C);  // AND_Gate
  or or_1 (Q, and_4_out, and_3_out, and_2_out, and_1_out);
endmodule
