// Logisim project jja54_lab8.circ as structural Verilog
module Register_File (
  input  CLK,
  input  [15:0] Data,
  input  WE,
  input  [2:0] rd,
  input  [2:0] rs,
  input  [2:0] rt,
  input  incr7,
  input  decr7,
  output [15:0] rs_out,
  output [15:0] rt_out
);

  wire demultiplexer_1_out0, demultiplexer_1_out1, demultiplexer_1_out2, demultiplexer_1_out3,
       demultiplexer_1_out4, demultiplexer_1_out5, demultiplexer_1_out6, demultiplexer_1_out7, or_1_out;
  wire [15:0] multiplexer_1_out, r0, r1, r2, r3, r4, r5, r6, r7, r7dec, r7inc, r7inpt, r7outp,
       subtractor_2_out;

  Demultiplexer #(.select(3)) demultiplexer_1 (
    .out0(demultiplexer_1_out0), .out1(demultiplexer_1_out1), .out2(demultiplexer_1_out2),
    .out3(demultiplexer_1_out3), .out4(demultiplexer_1_out4), .out5(demultiplexer_1_out5),
    .out6(demultiplexer_1_out6), .out7(demultiplexer_1_out7), .in(WE), .sel(rd));  // open: en
  or or_1 (or_1_out, demultiplexer_1_out7, incr7, decr7);
  Adder #(.width(16)) adder_1 (.a(r7outp), .b(16'h1), .out(r7inc));  // open: cin, cout
  Subtractor #(.width(16)) subtractor_1 (.a(r7outp), .b(16'h1), .out(r7dec));  // open: bin, bout
  Register #(.width(16)) register_1 (.D(Data), .en(demultiplexer_1_out0), .Q(r0), .clk(CLK));  // open: clr
  Register #(.width(16)) register_2 (.D(Data), .en(demultiplexer_1_out1), .Q(r1), .clk(CLK));  // open: clr
  Register #(.width(16)) register_3 (.D(Data), .en(demultiplexer_1_out2), .Q(r2), .clk(CLK));  // open: clr
  Register #(.width(16)) register_4 (.D(Data), .en(demultiplexer_1_out3), .Q(r3), .clk(CLK));  // open: clr
  Register #(.width(16)) register_5 (.D(Data), .en(demultiplexer_1_out4), .Q(r4), .clk(CLK));  // open: clr
  Register #(.width(16)) register_6 (.D(Data), .en(demultiplexer_1_out5), .Q(r5), .clk(CLK));  // open: clr
  Register #(.width(16)) register_7 (.D(Data), .en(demultiplexer_1_out6), .Q(r6), .clk(CLK));  // open: clr
  Register #(.width(16)) register_8 (.D(r7inpt), .en(or_1_out), .Q(r7outp), .clk(CLK));  // open: clr
  Multiplexer #(.width(16)) multiplexer_1 (.in0(Data), .in1(r7inc), .out(multiplexer_1_out), .sel(incr7));  // open: en
  Multiplexer #(.width(16)) multiplexer_2 (
    .in0(multiplexer_1_out), .in1(r7dec), .out(r7inpt), .sel(decr7));  // open: en
  Subtractor #(.width(16)) subtractor_2 (.a(r7outp), .b(16'h1), .out(subtractor_2_out));  // open: bin, bout
  Multiplexer #(.select(3), .width(16)) multiplexer_3 (
    .in0(r0), .in1(r1), .in2(r2), .in3(r3), .in4(r4), .in5(r5), .in6(r6), .in7(r7), .out(rs_out), .sel(rs));  // open: en
  Multiplexer #(.select(3), .width(16)) multiplexer_4 (
    .in0(r0), .in1(r1), .in2(r2), .in3(r3), .in4(r4), .in5(r5), .in6(r6), .in7(r7), .out(rt_out), .sel(rt));  // open: en
  Multiplexer #(.width(16)) multiplexer_5 (.in0(r7outp), .in1(subtractor_2_out), .out(r7), .sel(decr7));  // open: en
endmodule
